# Fritzing sketch ajolote (saved by Fritzing 0.9.2b)
breadboards: 2

parts:
  LED1 = smd LED [color="Infrared (940nm)" package="1206 [SMD]"]
  Parte1 = LED Matrix - Serial Interface - Red/Green/Blue
  Parte2 = LED Matrix - Serial Interface - Red/Green/Blue
  Parte3 = LED Matrix - Serial Interface - Red/Green/Blue
  Parte4 = LED Matrix - Serial Interface - Red/Green/Blue
  LED2 = smd LED [color="Blue (470nm)" package="1206 [SMD]"]
  Parte5 = Arduino Mega 2560 (Rev3)
  LED3 = smd LED [color="Blue (470nm)" package="1206 [SMD]"]
  LED4 = smd LED [color="Blue (470nm)" package="1206 [SMD]"]
  LED5 = smd LED [color="Blue (470nm)" package="1206 [SMD]"]
  LED6 = smd LED [color="Blue (470nm)" package="1206 [SMD]"]
  LED7 = smd LED [color="Blue (470nm)" package="1206 [SMD]"]
  R1 = Resistor [tolerance=±5% resistance=220 package=THT]
  R2 = Resistor [tolerance=±5% resistance=220 package=THT]
  R3 = Resistor [tolerance=±5% resistance=220 package=THT]
  R4 = Resistor [tolerance=±5% resistance=220 package=THT]
  R5 = Resistor [tolerance=±5% resistance=220 package=THT]
  R6 = Resistor [tolerance=±5% resistance=220 package=THT]
  R7 = Resistor [tolerance=±5% resistance=220 package=THT]
  LED8 = smd LED [color="Infrared (940nm)" package="1206 [SMD]"]
  LED9 = smd LED [color="Infrared (940nm)" package="1206 [SMD]"]
  LED10 = smd LED [color="Infrared (940nm)" package="1206 [SMD]"]
  LED11 = smd LED [color="Infrared (940nm)" package="1206 [SMD]"]
  LED12 = smd LED [color="Infrared (940nm)" package="1206 [SMD]"]
  R8 = Resistor [tolerance=±5% resistance=220 package=THT]
  R9 = Resistor [tolerance=±5% resistance=220 package=THT]
  R10 = Resistor [tolerance=±5% resistance=220 package=THT]
  R11 = Resistor [tolerance=±5% resistance=220 package=THT]
  R12 = Resistor [tolerance=±5% resistance=220 package=THT]

nets:
  VCC: LED1.cathode, Parte1.VCC, Parte2.VCC, Parte3.VCC, Parte5.5V, LED8.cathode, LED9.cathode, LED10.cathode, LED11.cathode, LED12.cathode
  N1: LED1.anode, Parte5.A5, R7.Pin_0
  N2: Parte1.SCK, Parte1.CS, Parte2.SCK, Parte2.CS, Parte3.SCK, Parte3.CS, Parte4.VCC, LED2.cathode, Parte5.D12_PWM, LED3.cathode, LED4.cathode, LED5.cathode, LED6.cathode, LED7.cathode, R7.Pin_1, R8.Pin_1, R9.Pin_1, R10.Pin_1, R11.Pin_1, R12.Pin_1
  N3: Parte1.MISO, Parte2.MOSI
  N4: Parte2.MISO, Parte3.MOSI
  GND: Parte2.GND, Parte3.GND, Parte4.CS
  N5: Parte3.MISO, Parte4.SCK
  N6: LED2.anode, R1.Pin_1
  N7: Parte5.A0, LED12.anode, R12.Pin_0
  N8: Parte5.A1, LED11.anode, R11.Pin_0
  N9: Parte5.A2, LED10.anode, R10.Pin_0
  N10: Parte5.A3, LED9.anode, R9.Pin_0
  N11: Parte5.A4, LED8.anode, R8.Pin_0
  N12: Parte5.D31, R1.Pin_0, R2.Pin_0, R3.Pin_0, R4.Pin_0, R5.Pin_0, R6.Pin_0
  N13: LED3.anode, R2.Pin_1
  N14: LED4.anode, R3.Pin_1
  N15: LED5.anode, R4.Pin_1
  N16: LED6.anode, R5.Pin_1
  N17: LED7.anode, R6.Pin_1
